// Digital circuit 1bit_full_adder.dig as structural Verilog
module _1bit_full_adder (
  input  A,
  input  B,
  input  Cin,
  output Sum,
  output Cout
);

  wire and_1_out, and_2_out, and_3_out, and_4_out, and_5_out, and_6_out, and_7_out, not_1_out, not_2_out,
       not_3_out;

  not not_1 (not_1_out, A);
  not not_2 (not_2_out, B);
  not not_3 (not_3_out, Cin);
  and and_1 (and_1_out, B, A);
  and and_2 (and_2_out, Cin, A);
  and and_3 (and_3_out, Cin, B);
  xor xor_1 (Cout, and_3_out, and_2_out, and_1_out);
  and and_4 (and_4_out, A, not_2_out, not_3_out);
  and and_5 (and_5_out, not_1_out, B, not_3_out);
  and and_6 (and_6_out, not_1_out, not_2_out, Cin);
  and and_7 (and_7_out, A, Cin, B);
  or or_1 (Sum, and_4_out, and_5_out, and_6_out, and_7_out);

  // Notes on the sheet:
  //   Cin: default 1
endmodule

/* Test case:
A   B   Cin   Sum   Cout
0   0   0          0     0
0   1   0          1     0
1   0   0          1     0
1   1   0          0     1
0   0   1          1     0
0   1   1          0     1
1   0   1          0     1
1   1   1          1     1
*/
