// Digital circuit 4-bit SLT.dig as structural Verilog
module _4_bit_SLT (
  input  [3:0] A,
  input  [3:0] B,
  output Out,
  output [3:0] _4Bit
);

  wire [3:0] slt_1_out;

  SLT slt_1 (.A(A[0]), .B(B[0]), .OUT(slt_1_out[0]));
  SLT slt_2 (.A(A[1]), .B(B[1]), .OUT(slt_1_out[1]));
  SLT slt_3 (.A(A[2]), .B(B[2]), .OUT(slt_1_out[2]));
  SLT slt_4 (.A(A[3]), .B(B[3]), .OUT(slt_1_out[3]));
  or or_1 (Out, slt_1_out[0], slt_1_out[1], slt_1_out[2], slt_1_out[3]);
  Div #(.Signed("true"), .Bits(4)) div_1 (.a(slt_1_out), .b(slt_1_out), .q(_4Bit));  // open: r
endmodule

/* Test case:
A	B	Out	4Bit
0x0	0x0	0	0
0x1	0x2	1	1
0x7	0xA	1	1
0xF	0xF	0	0
0x8	0x9	1	1
0xC	0x4	0	0
0x2	0x2	0	0
0x6	0x7	1	1
0x3	0x8	1	1
*/
