// Digital circuit 4-bit_AND.dig as structural Verilog
module _4_bit_AND (
  input  [3:0] A,
  input  [3:0] B,
  output [3:0] AND
);

  and and_1 (AND[0], A[0], B[0]);
  and and_2 (AND[1], A[1], B[1]);
  and and_3 (AND[2], A[2], B[2]);
  and and_4 (AND[3], A[3], B[3]);
endmodule

/* Test case:
A    B    AND
0x0  0x0  0x0
0xF  0xF  0xF
0x5  0x3  0x1
0xA  0x5  0x0
0xC  0x3  0x0
0x7  0x1  0x1
0x9  0x6  0x0
0xE  0x2  0x2
0xB  0x9  0x9
0xD  0xE  0xC
*/
