// Digital circuit 4-bit_OR.dig as structural Verilog
module _4_bit_OR (
  input  [3:0] A,
  input  [3:0] B,
  output [3:0] OR
);

  or or_1 (OR[0], A[0], B[0]);
  or or_2 (OR[1], A[1], B[1]);
  or or_3 (OR[2], A[2], B[2]);
  or or_4 (OR[3], A[3], B[3]);
endmodule

/* Test case:
A    B    OR
0x0  0x0  0x0
0xF  0xF  0xF
0x5  0x3  0x7
0xA  0x5  0xF
0xC  0x3  0xF
0x7  0x1  0x7
0x9  0x6  0xF
0xE  0x2  0xE
0xB  0x9  0xB
0xD  0xE  0xF
*/
