// Digital circuit 4-bit_XOR.dig as structural Verilog
module _4_bit_XOR (
  input  [3:0] A,
  input  [3:0] B,
  output [3:0] XOR
);

  xor xor_1 (XOR[0], A[0], B[0]);
  xor xor_2 (XOR[1], A[1], B[1]);
  xor xor_3 (XOR[2], A[2], B[2]);
  xor xor_4 (XOR[3], A[3], B[3]);
endmodule

/* Test case:
A    B    XOR
0x0  0x0  0x0
0xF  0xF  0x0
0x5  0x3  0x6
0xA  0x5  0xF
0xC  0x3  0xF
0x7  0x1  0x6
0x9  0x6  0xF
0xE  0x2  0xC
0xB  0x9  0x2
0xD  0xE  0x3
*/
