// Digital circuit 4-bit_ZeroFlag.dig as structural Verilog
module _4_bit_ZeroFlag (
  input  [3:0] in,
  output Out
);

  nor nor_1 (Out, in[0], in[1], in[2], in[3]);
  LED led_1 (.in(Out));
endmodule
