// Digital circuit 4bit_ALU.dlogic.dig as structural Verilog
module _4bit_ALU_dlogic (
  input  [3:0] A,
  input  [3:0] B,
  input  [2:0] Control,
  output Overflow,
  output Zero_Flag,
  output SLT_Logic,
  output [3:0] Expected_Result
);

  wire [3:0] _4_bit_and_1_and, _4_bit_or_1_or, _4_bit_slt_1__4bit, _4_bit_xor_1_xor, _4bit_full_adder_1_sum,
       _4bit_subtractor_1_sum;

  _4bit_full_adder _4bit_full_adder_1 (.A(A), .B(B), .Sum(_4bit_full_adder_1_sum), .Cout(Overflow));
  _4bit_subtractor _4bit_subtractor_1 (.B(B), .A(A), .Sum(_4bit_subtractor_1_sum));
  _4_bit_AND _4_bit_and_1 (.A(A), .B(B), .AND(_4_bit_and_1_and));
  _4_bit_OR _4_bit_or_1 (.A(A), .B(B), .OR(_4_bit_or_1_or));
  _4_bit_XOR _4_bit_xor_1 (.A(A), .B(B), .XOR(_4_bit_xor_1_xor));
  _4_bit_SLT _4_bit_slt_1 (.A(A), .B(B), .Out(SLT_Logic), ._4Bit(_4_bit_slt_1__4bit));
  Multiplexer #(.Selector_Bits(3), .Bits(4)) multiplexer_1 (
    .sel(Control), .in_0(_4bit_full_adder_1_sum), .in_1(_4bit_subtractor_1_sum), .in_2(_4_bit_and_1_and),
    .in_3(_4_bit_or_1_or), .in_4(_4_bit_xor_1_xor), .in_5(_4_bit_slt_1__4bit), .in_6(4'b0000),
    .in_7(4'b0000), .out(Expected_Result));
  _4_bit_ZeroFlag _4_bit_zeroflag_1 (.in(Expected_Result), .Out(Zero_Flag));
endmodule

/* Test case:
Control	A	B	Expected_Result   Zero_Flag	Overflow
0    	0x3	0x4 	 0x7              0         	0
0 	0xF  	0x1 	 0x0              1         	1
1  	0x5  	0x3 	 0x2              0         	0
1  	0x2  	0x2 	 0x0              1         	0
2  	0xA  	0x5 	 0x0              1          	0 
2   	0xF  	0x3 	 0x3              0           	1
3   	0x7  	0x8 	 0xF              0           	0
3   	0x0  	0x0 	 0x0              1           	0
4   	0x6  	0x3 	 0x5              0           	0
4	0x9  	0x9 	 0x0              1           	1
5  	0x3  	0x4 	 0x1              0           	0
5   	0x5  	0x4 	 0x0              1           	0
*/
