// Digital circuit 4bit_full_adder.dig as structural Verilog
module _4bit_full_adder (
  input  [3:0] A,
  input  [3:0] B,
  output [3:0] Sum,
  output Cout
);

  wire _1bit_full_adder_1_cout, _1bit_full_adder_2_cout, _1bit_full_adder_3_cout;

  _1bit_full_adder _1bit_full_adder_1 (.A(A[0]), .B(B[0]), .Cin(1'b0), .Sum(Sum[0]), .Cout(_1bit_full_adder_1_cout));
  _1bit_full_adder _1bit_full_adder_2 (
    .A(A[1]), .B(B[1]), .Cin(_1bit_full_adder_1_cout), .Sum(Sum[1]), .Cout(_1bit_full_adder_2_cout));
  _1bit_full_adder _1bit_full_adder_3 (
    .A(A[2]), .B(B[2]), .Cin(_1bit_full_adder_2_cout), .Sum(Sum[2]), .Cout(_1bit_full_adder_3_cout));
  _1bit_full_adder _1bit_full_adder_4 (.A(A[3]), .B(B[3]), .Cin(_1bit_full_adder_3_cout), .Sum(Sum[3]), .Cout(Cout));
endmodule

/* Test case:
A       B       Sum    Cout
0x0  0x0  0x0            0
0x1  0x1  0x2            0
0x7  0x1  0x8            0
0xF  0x1  0x0            1
0xA  0x5  0xF            0
0xD  0x3  0x0            1
0x9  0x6  0xF            0
0x9  0x9  0x2            1
0x4  0x4  0x8            0
0xF  0xF  0xE            1
*/
