// Digital circuit 4bit_subtractor.dig as structural Verilog
module _4bit_subtractor (
  input  [3:0] B,
  input  [3:0] A,
  output [3:0] Sum
);

  wire _1bit_full_adder_1_cout, _1bit_full_adder_2_cout, _1bit_full_adder_3_cout, and_1_out, and_2_out,
       and_3_out, and_4_out, not_1_out, not_2_out, not_3_out, not_4_out;

  not not_1 (not_1_out, B[0]);
  not not_2 (not_2_out, B[1]);
  not not_3 (not_3_out, B[2]);
  not not_4 (not_4_out, B[3]);
  and and_1 (and_1_out, not_1_out, 1'b1);
  and and_2 (and_2_out, not_2_out, 1'b1);
  and and_3 (and_3_out, not_3_out, 1'b1);
  and and_4 (and_4_out, not_4_out, 1'b1);
  _1bit_full_adder _1bit_full_adder_1 (
    .A(A[0]), .B(and_1_out), .Cin(1'b1), .Sum(Sum[0]), .Cout(_1bit_full_adder_1_cout));
  _1bit_full_adder _1bit_full_adder_2 (
    .A(A[1]), .B(and_2_out), .Cin(_1bit_full_adder_1_cout), .Sum(Sum[1]), .Cout(_1bit_full_adder_2_cout));
  _1bit_full_adder _1bit_full_adder_3 (
    .A(A[2]), .B(and_3_out), .Cin(_1bit_full_adder_2_cout), .Sum(Sum[2]), .Cout(_1bit_full_adder_3_cout));
  _1bit_full_adder _1bit_full_adder_4 (
    .A(A[3]), .B(and_4_out), .Cin(_1bit_full_adder_3_cout), .Sum(Sum[3]));  // open: Cout
endmodule

/* Test case:
A    B    Sum
0x0  0x0  0x0
0x1  0x1  0x0
0x7  0x1  0x6
0x1  0x7  0xA
0xA  0x5  0x5
0x5  0xA  0xB
0xF  0x8  0x7
0x8  0xF  0x9
0x4  0x4  0x0
0xF  0xF  0x0
*/
