// Digital circuit SLT.dig as structural Verilog
module SLT (
  input  A,
  input  B,
  output OUT
);

  wire not_1_out;

  not not_1 (not_1_out, A);
  and and_1 (OUT, not_1_out, B);
endmodule

/* Test case:
A    B    OUT
0x0  0x0  0x0
0x1  0x2  0x2
0x3  0x3  0x0
0x4  0x5  0x1
0x7  0x6  0x0
0xA  0x5  0x1
0x5  0xA  0xA
0x8  0x8  0x0
0x0  0xF  0x1
0xF  0x0  0x0
*/
